# Fritzing sketch semaforo (saved by Fritzing 0.9.2b)
breadboards: 1

parts:
  Part1 = Arduino Uno (Rev3)
  R1 = Resistor [tolerance=±5% resistance=220 package=THT]  # not connected
  R2 = Resistor [tolerance=±5% resistance=220 package=THT]
  R3 = Resistor [tolerance=±5% resistance=220 package=THT]
  LED1 = LED - 5mm [color="Green (555nm)" package="5 mm [THT]"]
  LED2 = LED - 5mm [color="Yellow (585nm)" package="5 mm [THT]"]
  LED3 = LED - 5mm [color="Red (633nm)" package="5 mm [THT]"]

nets:
  N1: Part1.D11_PWM/MOSI, LED1.anode
  N2: Part1.D12/MISO, LED2.anode
  N3: Part1.D13/SCK, LED3.anode
  N4: Part1.GND, R2.Pin_1, R3.Pin_1
  N5: R2.Pin_0, LED2.cathode
  N6: R3.Pin_0, LED1.cathode
