# Fritzing sketch led_pulsante (saved by Fritzing 0.9.0b)
breadboards: 1

parts:
  LED1 = LED - 5mm [color="Red (633nm)" package="5 mm [THT]"]
  R1 = Resistor [tolerance=±5% resistance=220 package=THT]
  Part1 = Arduino Uno (Rev3) - ICSP

nets:
  N1: LED1.cathode, Part1.GND
  N2: LED1.anode, R1.Pin_1
  N3: R1.Pin_0, Part1.D3_PWM
